# Fritzing sketch Microcontrollers schematic (saved by Fritzing 0.9.4)
breadboards: 1

parts:
  Part1 = Arduino Mega 2560 (Rev3)
  U2 = prefix0000
  8_Channel_Relay1 = 8 Channel Power Relay
  Mod1 = Raspberry Pi 4B
  DHT1 = DHT22 Humidity and Temperature Sensor
  Part2 = Adafruit CCS811
  BAT2 = 12 battery [package=battery]
  M4 = Stepper Motor - Bipolar
  U3 = prefix0000
  U4 = prefix0000
  M5 = Stepper Motor - Bipolar
  M6 = Stepper Motor - Bipolar
  HC-SR04_Sensor_1 = HC-SR04 Ultrasonic Distance Sensor

nets (from the breadboard view):
  GND: Part1.GND, HC-SR04_Sensor_1.GND
  N1: Part1.D12_PWM, U4.connector8
  N2: Part1.D11_PWM, U4.connector10
  N3: Part1.D10_PWM, U3.connector10
  N4: Part1.D9_PWM, U3.connector8
  N5: Part1.D8_PWM, U2.connector10
  5V: Part1.5V, U2.connector9, U2.connector11, U3.connector9, U3.connector11, U4.connector9, U4.connector11, HC-SR04_Sensor_1.VCC
  N6: Part1.D7_PWM, U2.connector8
  N7: Part1.D40, HC-SR04_Sensor_1.TRIG
  N8: Part1.D52, HC-SR04_Sensor_1.ECHO
  N9: U2.connector0, M4.D
  N10: U2.connector1, M4.B
  N11: U2.connector2, M4.C
  N12: U2.connector3, M4.A
  N13: U2.connector4, 8_Channel_Relay1.NC, U3.connector4, U4.connector4
  N14: U2.connector5, BAT2.-, U3.connector5, U4.connector5
  GND_2: 8_Channel_Relay1.GND, Mod1.GND, DHT1.GND, Part2.GND, Part2.!WAKE
  N15: 8_Channel_Relay1.IN1, Mod1.GPIO18
  N16: 8_Channel_Relay1.IN2, Mod1.GPIO23
  N17: 8_Channel_Relay1.IN3, Mod1.GPIO24
  N18: 8_Channel_Relay1.IN4, Mod1.GPIO25
  N19: 8_Channel_Relay1.IN5, Mod1.GPIO4
  VCC: 8_Channel_Relay1.VCC, Mod1.5V, DHT1.VDD, Part2.VIN
  N20: 8_Channel_Relay1.COM, BAT2.+
  N21: Mod1.GPIO2, Part2.SDA
  N22: Mod1.GPIO3, Part2.SCL
  N23: Mod1.GPIO17, DHT1.DATA
  N24: U3.connector0, M5.D
  N25: U3.connector1, M5.B
  N26: U3.connector2, M5.C
  N27: U3.connector3, M5.A
  N28: U4.connector0, M6.D
  N29: U4.connector1, M6.B
  N30: U4.connector2, M6.C
  N31: U4.connector3, M6.A

notes:
  GPIO18-->IN1 Air pump
  GPIO23-->IN2 Nutrient pump
  GPIO24-->IN3 Solenoid
  GPIO25-->IN4 Skylark LEDs
  GPIO4-->IN5 Motor Drivers
  GPIO18-->IN1 Air pump
  GPIO23-->IN2 Nutrient pump
  GPIO24-->IN3 Solenoid
  GPIO25-->IN4 Skylark LEDs
  Limit Switch Pins:
  2, 3, 18, 19, 20, 21
  Limit Switch Pins:
  2, 3, 18, 19, 20, 21
  THERE IS NO SCHEMATIC PART
  AVAILABLE FOR THIS DEVICE
  24V Power Supply

custom parts:
  8 Channel Power Relay: An 8 channel power relay. The module operates at 5V.
  12 battery: 12V lead acid type battery, like the Husqvarna YTH2448 12V 35AH battery. This is the mini version 1/4 the size of the actual battery to be closer to typical breadboard parts (around 2in wide rathher than 7in). The pads in pcb are sized to accomidate up to 14ga wire (as these batterys will deliver high currents.)
  HC-SR04 Ultrasonic Distance Sensor: The HC-SR04 is an ultrasonic distance sensor. It is capable of providing measurement for ranges of 2cm to 400cm. The module operates at 5V.
